# Fritzing sketch lasermaze (saved by Fritzing 0.8.5b)
circuit board: 3.31611cm x 2.70933cm
breadboards: 1

parts:
  Part1 = Arduino Uno (Rev3)
  Sensor2 = Audio Jack (TRS) 3.5mm [package="4Ucon 08780 [THT]"]
  Sensor3 = Audio Jack (TRS) 3.5mm [package="4Ucon 08780 [THT]"]
  Sensor4 = Audio Jack (TRS) 3.5mm [package="4Ucon 08780 [THT]"]
  Sensor5 = Audio Jack (TRS) 3.5mm [package="4Ucon 08780 [THT]"]
  Gate_Laser = Audio Jack (TRS) 3.5mm [package="4Ucon 08780 [THT]"]
  Laser1 = Audio Jack (TRS) 3.5mm [package="4Ucon 08780 [THT]"]
  Laser2 = Audio Jack (TRS) 3.5mm [package="4Ucon 08780 [THT]"]
  Laser3 = Audio Jack (TRS) 3.5mm [package="4Ucon 08780 [THT]"]
  Laser4 = Audio Jack (TRS) 3.5mm [package="4Ucon 08780 [THT]"]
  Laser5 = Audio Jack (TRS) 3.5mm [package="4Ucon 08780 [THT]"]
  Gate_Sensor = Audio Jack (TRS) 3.5mm [package="4Ucon 08780 [THT]"]
  J1 = Piezo Speaker
  Sensor1 = Audio Jack (TRS) 3.5mm [package="4Ucon 08780 [THT]"]
  J2 = female pin header, 6 pins [form="♀ (female)"]

nets:
  N1: Part1.A0, Gate_Sensor.Ring, J2.pin1
  N2: Part1.A1, Sensor5.Ring, J2.pin2
  N3: Part1.A2, Sensor4.Ring, J2.pin3
  N4: Part1.A3, Sensor3.Ring, J2.pin4
  N5: Part1.D8, Part1.5V, Sensor2.Tip, Sensor3.Tip, Sensor4.Tip, Sensor5.Tip, Laser3.Ring, Gate_Sensor.Tip, Sensor1.Tip
  N6: Part1.D9_PWM, Laser2.Tip
  N7: Part1.D10_PWM/SS, Laser3.Tip
  N8: Part1.D11_PWM/MOSI, Laser4.Tip
  N9: Part1.D12/MISO, Laser5.Tip
  N10: Part1.D7, Gate_Laser.Tip
  N11: Part1.GND, Gate_Laser.Ring, Laser1.Ring, Laser2.Ring, Laser4.Ring, Laser5.Ring, J1.pin1
  N12: Sensor2.Ring, J2.pin5
  N13: Sensor1.Ring, J2.pin6
